# Fritzing sketch IR CONTROL CAR (saved by Fritzing 0.9.3b)

parts:
  IR1 = TSOP312.., 314.. [package=THT]
  IC1 = L293D [package=THT]
  Part1 = Arduino Uno (Rev3)
  M1 = DC Motor
  M2 = DC Motor
  BAT1 = BC9VPC [package=bc9vpc]
  IC3 = Voltage Regulator [package=78xxl]  # not connected

nets:
  GND: IR1.GND, Part1.GND
  N1: IR1.Vs, Part1.5V
  N2: IR1.Data, Part1.D12/MISO
  N3: IC1.Enable_1, IC1.In_1, IC1.Enable_2, Part1.D2
  N4: IC1.Out_1_(_Controlled_by_Enable_1_), M1.pin_1
  N5: IC1.Out_2_(_Controlled_by_Enable_1_), M1.pin_2
  N6: IC1.In_2, Part1.D3_PWM
  N7: IC1.+Vmotor, BAT1.V-
  N8: IC1.In_3, Part1.D4
  N9: IC1.Out_3_(_Controlled_by_Enable_2_), M2.pin_2
  N10: IC1.Out_4_(_Controlled_by_Enable_2_), M2.pin_1
  N11: IC1.In_4, IC1.+V, Part1.D5_PWM, BAT1.V+
